// Logisim project Logisim_file.circ as structural Verilog: 1 circuit, main circuit main
module main (
  input  in_1,
  input  [1:0] in_2,
  input  in_3,
  input  [7:0] in_4
);

  wire clock_1_out, decoder_1_out0, decoder_1_out1, decoder_1_out2, decoder_1_out3, shift_register_1_p3,
       t_ff_1_q;
  wire [1:0] counter_1_q;
  wire [7:0] adder_1_out, shift_register_1_p1;

  T_Flip_Flop t_ff_1 (.T(1'b1), .clk(clock_1_out), .Q(t_ff_1_q));  // open: Qn, reset, preset
  Clock clock_1 (.out(clock_1_out));
  Counter #(.max('h3), .width(2)) counter_1 (
    .load(in_1), .D(in_2), .count(1'b1), .Q(counter_1_q), .clk(t_ff_1_q));  // open: carry, up, clr
  Decoder #(.select(2)) decoder_1 (
    .out0(decoder_1_out0), .out1(decoder_1_out1), .out2(decoder_1_out2), .out3(decoder_1_out3),
    .sel(counter_1_q), .en(1'b1));
  Multiplexer #(.select(2), .width(4)) multiplexer_1 (.sel(counter_1_q));  // open: in0, in1, in2, in3, out
  _7_Segment_Display u_7_segment_display_1 ();  // open: g, f, a, b, e, d, c, dp
  _7_Segment_Display u_7_segment_display_2 ();  // open: g, f, a, b, e, d, c, dp
  _7_Segment_Display u_7_segment_display_3 ();  // open: g, f, a, b, e, d, c, dp
  // Shift_Register #(.length(16)) shift_register_1: pin names not known; wires that end beside it: shift_register_1_p1, in_3, shift_register_1_p3, 1'b1, clock_1_out, in_4[7], in_4[6], in_4[5], in_4[4], in_4[3], in_4[2], in_4[1], in_4[0]
  _7_Segment_Display u_7_segment_display_4 ();  // open: g, f, a, b, e, d, c, dp
  Adder adder_1 (.a(shift_register_1_p1), .out(adder_1_out));  // open: b, cin, cout
  Multiplexer #(.width(8)) multiplexer_2 (.in0(adder_1_out));  // open: in1, out, sel
endmodule
